// Logisim project arquitetura_de_computadores_22_02_2024.circ as structural Verilog: 5 circuits, main circuit main
module main (
  input  [3:0] in_1,
  input  [3:0] in_2,
  input  [3:0] in_3,
  input  [3:0] in_4,
  output out_5,
  output out_6
);

  // AD_1 ad_1_1: pin names not known; wires that end beside it: out_5, in_1, in_3, in_2, 1'b0
  // SUB_1 sub_1_1: pin names not known; wires that end beside it: out_6, in_1, in_4, in_2, 1'b0
endmodule

// AD-4
module AD_1 (
  input  A,
  input  B,
  input  Vem_1,
  output S,
  output Vai_1
);

  wire and_1_out, and_2_out, or_1_out, xor_1_out;

  xor xor_1 (xor_1_out, A, B);
  or or_1 (or_1_out, Vem_1, B);
  and and_1 (and_1_out, Vem_1, B);
  xor xor_2 (S, xor_1_out, Vem_1);
  and and_2 (and_2_out, or_1_out, A);
  or or_2 (Vai_1, and_2_out, and_1_out);
endmodule

module AD_4 (
  input  [3:0] in_1,
  input  [3:0] in_2,
  input  in_3,
  output out_4,
  output [3:0] out_5
);

  wire ad_1_2_vai_1, ad_1_3_vai_1, ad_1_4_vai_1;

  AD_1 ad_1_1 (.A(in_2[3]), .B(in_1[3]), .S(out_5[3]), .Vem_1(ad_1_2_vai_1), .Vai_1(out_4));
  AD_1 ad_1_2 (.A(in_2[2]), .B(in_1[2]), .S(out_5[2]), .Vem_1(ad_1_3_vai_1), .Vai_1(ad_1_2_vai_1));
  AD_1 ad_1_3 (.A(in_2[1]), .B(in_1[1]), .S(out_5[1]), .Vem_1(ad_1_4_vai_1), .Vai_1(ad_1_3_vai_1));
  AD_1 ad_1_4 (.A(in_2[0]), .B(in_1[0]), .S(out_5[0]), .Vem_1(in_3), .Vai_1(ad_1_4_vai_1));
endmodule

// SUB-4
module SUB_1 (
  input  A,
  input  B,
  input  Vem_1,
  output S,
  output Vai_1
);

  wire and_1_out, and_2_out, not_1_out, or_1_out, xor_1_out;

  not not_1 (not_1_out, A);
  xor xor_1 (xor_1_out, A, B);
  or or_1 (or_1_out, Vem_1, B);
  and and_1 (and_1_out, Vem_1, B);
  xor xor_2 (S, xor_1_out, Vem_1);
  and and_2 (and_2_out, or_1_out, not_1_out);
  or or_2 (Vai_1, and_2_out, and_1_out);
endmodule

module SUB_4 (
  input  [3:0] in_1,
  input  [3:0] in_2,
  input  in_3,
  output out_4,
  output [3:0] out_5
);

  wire sub_1_2_vai_1, sub_1_3_vai_1, sub_1_4_vai_1;

  SUB_1 sub_1_1 (.A(in_2[3]), .B(in_1[3]), .Vem_1(sub_1_2_vai_1), .S(out_5[3]), .Vai_1(out_4));
  SUB_1 sub_1_2 (.A(in_2[2]), .B(in_1[2]), .Vem_1(sub_1_3_vai_1), .S(out_5[2]), .Vai_1(sub_1_2_vai_1));
  SUB_1 sub_1_3 (.A(in_2[1]), .B(in_1[1]), .Vem_1(sub_1_4_vai_1), .S(out_5[1]), .Vai_1(sub_1_3_vai_1));
  SUB_1 sub_1_4 (.A(in_2[0]), .B(in_1[0]), .Vem_1(in_3), .S(out_5[0]), .Vai_1(sub_1_4_vai_1));
endmodule
